# Fritzing sketch esp01_dht11_schaltplan (saved by Fritzing 0.9.1b)
circuit board: 5.90786cm x 4.76955cm
breadboards: 1

parts:
  U1 = ESP8266 WiFi Module [part_number=ESP8266]
  DHT1 = DHT11 Humitidy and Temperature Sensor
  R1 = Resistor [tolerance=±5% resistance=10k package=THT]
  Power_plug1 = Power plug

nets:
  VCC: U1.VCC, U1.CH_PD, DHT1.VDD, R1.Pin_1, Power_plug1.VCC
  N1: U1.GPIO_0, DHT1.DATA, R1.Pin_0
  GND: U1.GND, DHT1.GND, Power_plug1.GND

notes:
  3.3V breadboard power supply
  ESP8266 can alternatively be connected to FTDI VCC 3.3V line.
  But that will not give enough power for WIFI or DHT.
  DHT11
  ESP8266 / ESP-01

custom parts:
  ESP8266 WiFi Module: Generic WiFi Module based on the ESP8266 with onboard PCB antenna and UART communications
  DHT11 Humitidy and Temperature Sensor: DHT11 Humidity and Temperature Sensor
